// Logisim project 28,09.circ as structural Verilog: 10 circuits, main circuit main
module main (
  input  in_1,
  input  in_2,
  input  in_3,
  input  in_4,
  input  in_5,
  input  in_6,
  input  in_7,
  input  in_8,
  output out_9,
  output out_10,
  output out_11,
  output out_12
);

  wire fulladder_1_carry, fulladder_2_carry, fulladder_3_carry;

  fulladder fulladder_1 (.Arg1(in_8), .Arg2(in_4), .Carry_in(1'b0), .Carry(fulladder_1_carry), .Result(out_12));
  fulladder fulladder_2 (
    .Arg1(in_7), .Arg2(in_3), .Carry_in(fulladder_1_carry), .Carry(fulladder_2_carry), .Result(out_11));
  fulladder fulladder_3 (
    .Arg1(in_6), .Arg2(in_2), .Carry_in(fulladder_2_carry), .Carry(fulladder_3_carry), .Result(out_10));
  fulladder fulladder_4 (.Arg1(in_5), .Arg2(in_1), .Carry_in(fulladder_3_carry), .Result(out_9));  // open: Carry
endmodule

module polusum (
  input  Arg1,
  input  Arg2,
  output Carry,
  output Result
);

  buf and_1 (Carry, Arg2);  // AND_Gate
  xor xor_1 (Result, Arg1, Arg2);
endmodule

module fulladder (
  input  Arg1,
  input  Arg2,
  input  Carry_in,
  output Carry,
  output Result
);

  wire polusum_1_carry, polusum_1_result, polusum_2_carry;

  polusum polusum_1 (.Arg1(Arg1), .Arg2(Arg2), .Carry(polusum_1_carry), .Result(polusum_1_result));
  polusum polusum_2 (.Arg1(polusum_1_result), .Arg2(Carry_in), .Carry(polusum_2_carry), .Result(Result));
  buf or_1 (Carry, polusum_2_carry);  // OR_Gate
endmodule

module Mux2to1 (
  input  in1,
  input  Sel,
  input  in2,
  output result
);

  wire nand_1_out, nand_2_out, not_1_out;

  not not_1 (not_1_out, Sel);
  nand nand_1 (nand_1_out, in1, not_1_out);
  nand nand_2 (nand_2_out, Sel, in2);
  not nand_3 (result, nand_2_out);  // NAND_Gate
endmodule

module Mux4to1 (
  input  in_1,
  input  in_2,
  input  [1:0] in_3,
  output out_4
);

  wire mux2to1_1_result, mux2to1_2_result;

  Mux2to1 mux2to1_1 (.in1(in_1), .Sel(in_3[0]), .in2(in_2), .result(mux2to1_1_result));
  Mux2to1 mux2to1_2 (.in1(in_1), .Sel(in_3[0]), .in2(in_2), .result(mux2to1_2_result));
  Mux2to1 mux2to1_3 (.in1(mux2to1_1_result), .Sel(in_3[1]), .in2(mux2to1_2_result), .result(out_4));
endmodule

module Decoder1B (
  input  Sel,
  output Out1,
  output Out2
);

  wire not_1_out;

  not not_1 (not_1_out, Sel);
  Pull_Resistor pull_resistor_1 (.node(Out1));
  assign Out1 = not_1_out ? 1'b1 : 1'bz;  // Controlled_Buffer controlled_buffer_1
  Pull_Resistor pull_resistor_2 (.node(Out2));
  assign Out2 = Sel ? 1'b1 : 1'bz;  // Controlled_Buffer controlled_buffer_2
endmodule

module Decoder4bit (
);

  wire controlled_buffer_1_out, controlled_buffer_2_out, controlled_buffer_3_out, controlled_buffer_4_out,
       decoder1b_1_out1, decoder1b_1_out2, decoder1b_2_out1, decoder1b_2_out2, not_1_out;

  assign controlled_buffer_1_out = not_1_out ? decoder1b_1_out1 : 1'bz;  // Controlled_Buffer controlled_buffer_1
  Decoder1B decoder1b_1 (.Sel(1'b1), .Out1(decoder1b_1_out1), .Out2(decoder1b_1_out2));
  assign controlled_buffer_2_out = not_1_out ? decoder1b_1_out2 : 1'bz;  // Controlled_Buffer controlled_buffer_2
  not not_1 (not_1_out, 1'b1);
  assign controlled_buffer_3_out = 1'b1 ? decoder1b_2_out1 : 1'bz;  // Controlled_Buffer controlled_buffer_3
  Decoder1B decoder1b_2 (.Sel(1'b1), .Out1(decoder1b_2_out1), .Out2(decoder1b_2_out2));
  assign controlled_buffer_4_out = 1'b1 ? decoder1b_2_out2 : 1'bz;  // Controlled_Buffer controlled_buffer_4
  Pull_Resistor pull_resistor_1 (.node(controlled_buffer_1_out));
  Pull_Resistor pull_resistor_2 (.node(controlled_buffer_2_out));
  Pull_Resistor pull_resistor_3 (.node(controlled_buffer_3_out));
  Pull_Resistor pull_resistor_4 (.node(controlled_buffer_4_out));
endmodule

module Arifmlogic (
  input  [7:0] in_1,
  input  [7:0] in_2,
  input  [1:0] in_3,
  input  in_4,
  output [7:0] out_5
);

  wire [7:0] adder_1_out, nand_1_out, subtractor_1_out, xor_1_out;

  Subtractor subtractor_1 (.a(in_2), .b(in_1), .out(subtractor_1_out));  // open: bin, bout
  Adder adder_1 (.a(in_2), .b(in_1), .out(adder_1_out));  // open: cin, cout
  assign nand_1_out = ~(in_2 & in_1);  // NAND_Gate nand_1, 8 bits wide
  assign xor_1_out = in_2 ^ in_1;  // XOR_Gate xor_1, 8 bits wide
  Multiplexer #(.select(2)) multiplexer_1 (
    .in0(adder_1_out[0]), .in1(subtractor_1_out[0]), .in2(xor_1_out[0]), .in3(nand_1_out[0]), .out(out_5[0]),
    .sel(in_3));
  // Pins of 1 and 8 bits meet at out_5
  // Pins of 1 and 8 bits meet at nand_1_out
  // Pins of 1 and 8 bits meet at xor_1_out
  // Pins of 1 and 8 bits meet at adder_1_out
  // Pins of 1 and 8 bits meet at subtractor_1_out
endmodule

module SRLatch (
  input  in_1,
  input  in_2,
  output out_3
);

  wire nand_2_out;

  nand nand_1 (out_3, in_1, nand_2_out);
  nand nand_2 (nand_2_out, out_3, in_2);
endmodule

module BitRegister (
  input  in_1,
  input  in_2,
  input  in_3,
  output out_4
);

  wire and_1_out, nand_1_out, nand_2_out, nand_4_out, not_1_out;

  and and_1 (and_1_out, in_2, in_3);
  not not_1 (not_1_out, in_1);
  nand nand_1 (nand_1_out, in_1, and_1_out);
  nand nand_2 (nand_2_out, and_1_out, not_1_out);
  not nand_3 (out_4, nand_1_out);  // NAND_Gate
  nand nand_4 (nand_4_out, out_4, nand_2_out);
endmodule
